# Fritzing sketch CANDLE-BLE-BASE (saved by Fritzing 0.9.10b)
circuit board: 9.5cm x 9cm
breadboards: 1

parts:
  LOLIN32_LITE = Wemos Lolin32lite
  R1 = Resistor [tolerance=±5% power=0.25 resistance=2.2k package=THT]
  BUS_I2C = shrouded pin header, 6 pins [form="♂ (shrouded male)"]
  R2 = Resistor [tolerance=±5% power=0.25 resistance=2.2k package=THT]
  R3 = Resistor [tolerance=±5% power=0.25 resistance=10k package=THT]
  R4 = Resistor [tolerance=±5% power=0.25 resistance=10k package=THT]
  R5 = Resistor [tolerance=±5% power=0.25 resistance=10k package=THT]
  R6 = Resistor [tolerance=±5% power=0.25 resistance=10k package=THT]
  R7 = Resistor [tolerance=±5% power=0.25 resistance=10k package=THT]
  ROUE_CODEUSE = KF142R-5.08-2P [package="Clamp Terminal Bloc"]
  J3 = KF142R-5.08-2P [package="Clamp Terminal Bloc"]
  JOYSTICK = KF142R-5.08-3P [package="Clamp Terminal Bloc"]
  BOOST_5V = female pin header, 3 pins [form="♀ (female)"]
  R10 = Resistor [tolerance=±5% power=0.25 resistance=3.3k package=THT]
  R11 = Resistor [tolerance=±5% power=0.25 resistance=4.7k package=THT]
  R12 = Resistor [tolerance=±5% power=0.25 resistance=4.7k package=THT]
  R13 = Resistor [tolerance=±5% power=0.25 resistance=3.3k package=THT]
  J5 = KF142R-5.08-2P [package="Clamp Terminal Bloc"]
  18560 = battery_holder_single_18650
  BATT = female pin header, 2 pins [form="♀ (female)"]
  SEND = KF142R-5.08-2P [package="Clamp Terminal Bloc"]
  R14 = Resistor [tolerance=±5% power=0.25 resistance=10k package=THT]
  R15 = Resistor [tolerance=±5% power=0.25 resistance=10k package=THT]
  ON/SYNCHRO = KF142R-5.08-2P [package="Clamp Terminal Bloc"]
  R16 = Resistor [tolerance=±5% power=0.25 resistance=100k package=THT]
  R17 = Resistor [tolerance=±5% power=0.25 resistance=100k package=THT]

nets:
  SEND/OFF: LOLIN32_LITE.pin_4, SEND.pin1, SEND.pin3, R15.Pin_0
  ON/SYNCHRO: LOLIN32_LITE.pin_5, R14.Pin_0, ON/SYNCHRO.pin1, ON/SYNCHRO.pin3
  BAS: LOLIN32_LITE.pin_6, R4.Pin_0, J5.pin1, J5.pin3
  DROITE: LOLIN32_LITE.pin_7, R5.Pin_0, JOYSTICK.pin3, JOYSTICK.pin_6
  HAUT: LOLIN32_LITE.pin_8, R6.Pin_0, JOYSTICK.pin2, JOYSTICK.pin_5
  GAUCHE: LOLIN32_LITE.pin_9, R7.Pin_0, JOYSTICK.pin1, JOYSTICK.pin_4
  A CODEUSE: LOLIN32_LITE.pin_10, R10.Pin_1, R11.Pin_0
  B CODEUSE: LOLIN32_LITE.pin_11, R12.Pin_0, R13.Pin_1
  V BATT: LOLIN32_LITE.pin_12, R16.Pin_0, R17.Pin_0
  GND: LOLIN32_LITE.pin_13, BUS_I2C.pin6, R4.Pin_1, R5.Pin_1, R6.Pin_1, R7.Pin_1, ROUE_CODEUSE.pin2, ROUE_CODEUSE.pin4, BOOST_5V.pin2, R11.Pin_1, R12.Pin_1, R14.Pin_1, R15.Pin_1, R17.Pin_1
  INT: LOLIN32_LITE.pin_16, BUS_I2C.pin4, R3.Pin_0
  SCL: LOLIN32_LITE.pin_19, R1.Pin_1, BUS_I2C.pin3
  SDA: LOLIN32_LITE.pin_20, BUS_I2C.pin2, R2.Pin_1
  3.3V: LOLIN32_LITE.pin_28, R1.Pin_0, BUS_I2C.pin1, R2.Pin_0, R3.Pin_1, BOOST_5V.pin1, J5.pin2, J5.pin4, SEND.pin2, SEND.pin4, ON/SYNCHRO.pin2, ON/SYNCHRO.pin4
  N1: ROUE_CODEUSE.pin1, ROUE_CODEUSE.pin3, BOOST_5V.pin3
  N2: J3.pin1, J3.pin3, R10.Pin_0
  N3: J3.pin2, J3.pin4, R13.Pin_0
  + BATT: 18560.+#0, BATT.pin1, R16.Pin_1
  - BATT: 18560.+#1, BATT.pin2

notes:
  +  -
  1  2  3  4  5
  6  7
  8  9
  10 11 12 13
  BY SMHOSY
  +
  CANDLE-BLE V1.0

custom parts:
  Wemos Lolin32lite: Wemos Lolinlite32 wifi and blue tooth board based on the ESP-32 cpu, digital I/Os 19, analog inputs 6, clock 240mhz, Flash 4Mbytes, lipo battery charger (500ma connection broken out on breadboard but not pcb), usb.
  KF142R-5.08-2P: 5.08mm 14 ~ 22 awg 15A Trou traversant 250V 4 Push-Pull, P = 5.08mm Système de serrage à ressort Bornier ROHS
  KF142R-5.08-3P: 5.08mm 14 ~ 22 awg 15A Trou traversant 250V 4 Push-Pull, P = 5.08mm Système de serrage à ressort Bornier ROHS
  battery_holder_single_18650: single 18650 battery holder
