# Fritzing sketch CANDLE-BLE-BP-AXE-CDM (saved by Fritzing 0.9.10b)
circuit board: 14.6cm x 3.49999cm
breadboards: 1

parts:
  U1 = PCF8574 [package="DIP16 [THT]"]
  LED1 = LED - 3mm [color="Red (633nm)" current=0.030 package="3 mm [THT]"]
  LED2 = LED - 3mm [color="Green (570nm)" current=0.030 package="3 mm [THT]"]
  LED3 = LED - 3mm [color="Green (570nm)" current=0.030 package="3 mm [THT]"]
  P4 = MY PAD [package=NONE]
  R7 = Resistor [tolerance=±5% resistance=10k power=0.25 package="1206 [SMD]"]
  P3 = MY PAD [package=NONE]
  R6 = Resistor [tolerance=±5% resistance=10k power=0.25 package="1206 [SMD]"]
  P2 = MY PAD [package=NONE]
  R5 = Resistor [tolerance=±5% resistance=10k power=0.25 package="1206 [SMD]"]
  P2-1 = MY PAD [package=NONE]
  R4 = Resistor [tolerance=±5% resistance=10k power=0.25 package="1206 [SMD]"]
  P1 = MY PAD [package=NONE]
  R3 = Resistor [tolerance=±5% resistance=680 power=0.25 package="1206 [SMD]"]
  R2 = Resistor [tolerance=±5% resistance=680 power=0.25 package="1206 [SMD]"]
  R1 = Resistor [tolerance=±5% resistance=680 power=0.25 package="1206 [SMD]"]
  J1 = double row smd male pin header, 6 pins [form="♂ (male)"]
  Pad1 = Pad [width=2 height=1 connect=center]
  Pad5 = Pad [width=2 height=1 connect=center]
  Pad6 = Pad [width=2 height=1 connect=center]
  Pad7 = Pad [width=2 height=1 connect=center]
  Pad8 = Pad [width=2 height=1 connect=center]
  Pad9 = Pad [width=2 height=1 connect=center]
  Pad10 = Pad [width=0.1 height=0.1 connect=center]  # not connected
  Pad11 = Pad [width=0.1 height=0.1 connect=center]  # not connected

nets:
  GND: U1.A0, U1.A2, U1.GND, P2-1.MOUNT, J1.pin6, Pad1.pad, Pad6.pad
  3.3V: U1.A1, U1.VCC, R7.Pin_1, R6.Pin_1, R5.Pin_1, R4.Pin_1, R3.Pin_1, R2.Pin_1, R1.Pin_1, J1.pin1, Pad5.pad, Pad9.pad
  BP SELECT AXE: U1.P0, R4.Pin_0, P1.MOUNT
  LED AXE X: U1.P1, LED1.cathode
  LED AXE Y: U1.P2, LED2.cathode
  LED AXE Z: U1.P3, LED3.cathode
  BP HOMING: U1.P4, P4.MOUNT, R7.Pin_0
  BP INIT ZERO Z: U1.P5, P3.MOUNT, R6.Pin_0
  BP INIT ZERO XY: U1.P6, P2.MOUNT, R5.Pin_0
  INT: U1.INT, J1.pin4, Pad7.pad, Pad8.pad
  SCL: U1.SCL, J1.pin3
  SDA: U1.SDA, J1.pin2
  N1: LED1.anode, R1.Pin_0
  N2: LED2.anode, R2.Pin_0
  N3: LED3.anode, R3.Pin_0

notes:
  CANDLE-BLE
  BP AXE
  BY SMHOSY
  +

custom parts:
  MY PAD: StarbBoard Power pad Power pads are designated by the star cutout in the top layer.
