# Fritzing sketch CANDLE-BLE-BP-SCENE-CDM (saved by Fritzing 0.9.10b)
circuit board: 14.6cm x 2.79999cm
breadboards: 1

parts:
  U1 = PCF8574 [package="DIP16 [THT]"]
  U2 = PCF8574 [package="DIP16 [THT]"]
  J1 = double row smd male pin header, 6 pins [form="♂ (male)"]
  R1 = Resistor [tolerance=±5% resistance=10 power=0.25 package="1206 [SMD]"]
  R2 = Resistor [tolerance=±5% resistance=10 power=0.25 package="1206 [SMD]"]
  P3 = MY PAD [package=NONE]
  R3 = Resistor [tolerance=±5% resistance=10 power=0.25 package="1206 [SMD]"]
  P6 = MY PAD [package=NONE]
  P4 = MY PAD [package=NONE]
  P5 = MY PAD [package=NONE]
  R5 = Resistor [tolerance=±5% resistance=10 power=0.25 package="1206 [SMD]"]
  R6 = Resistor [tolerance=±5% resistance=10 power=0.25 package="1206 [SMD]"]
  R4 = Resistor [tolerance=±5% resistance=10 power=0.25 package="1206 [SMD]"]
  P2-1 = MY PAD [package=NONE]
  P2 = MY PAD [package=NONE]
  P12 = MY PAD [package=NONE]
  P9 = MY PAD [package=NONE]
  P7 = MY PAD [package=NONE]
  P11 = MY PAD [package=NONE]
  P8 = MY PAD [package=NONE]
  P10 = MY PAD [package=NONE]
  R10 = Resistor [tolerance=±5% resistance=10 power=0.25 package="1206 [SMD]"]
  R12 = Resistor [tolerance=±5% resistance=10 power=0.25 package="1206 [SMD]"]
  R9 = Resistor [tolerance=±5% resistance=10 power=0.25 package="1206 [SMD]"]
  R7 = Resistor [tolerance=±5% resistance=10 power=0.25 package="1206 [SMD]"]
  R8 = Resistor [tolerance=±5% resistance=10 power=0.25 package="1206 [SMD]"]
  R11 = Resistor [tolerance=±5% resistance=10 power=0.25 package="1206 [SMD]"]
  P2-2 = MY PAD [package=NONE]
  P1 = MY PAD [package=NONE]
  Pad1 = Pad [width=1 height=2 connect=center]
  Pad2 = Pad [width=1 height=2 connect=center]
  Pad3 = Pad [width=1 height=2 connect=center]
  Pad4 = Pad [width=1 height=2 connect=center]
  Pad5 = Pad [width=1 height=2 connect=center]
  Pad6 = Pad [width=1 height=2 connect=center]
  Pad9 = Pad [width=1 height=2 connect=center]
  Pad10 = Pad [width=1 height=2 connect=center]
  Pad11 = Pad [width=1 height=2 connect=center]
  Pad12 = Pad [width=1 height=2 connect=center]
  Pad13 = Pad [width=1 height=2 connect=center]
  Pad14 = Pad [width=1 height=2 connect=center]
  Pad15 = Pad [width=1 height=2 connect=center]
  Pad16 = Pad [width=1 height=2 connect=center]
  Pad17 = Pad [width=0.1 height=0.1 connect=center]  # not connected
  Pad18 = Pad [width=0.1 height=0.1 connect=center]  # not connected

nets:
  3.3V: U1.A0, U1.A1, U1.VCC, U2.A2, U2.VCC, J1.pin1, R1.Pin_0, R2.Pin_0, R3.Pin_0, R5.Pin_0, R6.Pin_0, R4.Pin_0, R10.Pin_0, R12.Pin_0, R9.Pin_0, R7.Pin_0, R8.Pin_0, R11.Pin_0
  GND: U1.A2, U1.GND, U2.A0, U2.A1, U2.GND, J1.pin6, P2-1.MOUNT, P2-2.MOUNT, Pad15.pad, Pad16.pad
  BP SCENE 2: U1.P0, R2.Pin_1, P2.MOUNT
  BP SCENE 1: U1.P1, R1.Pin_1, P1.MOUNT
  BP PROBE 1: U1.P2, P7.MOUNT, R7.Pin_1
  BP PROBE 2: U1.P3, P8.MOUNT, R8.Pin_1
  BP PROBE 3: U1.P4, P9.MOUNT, R9.Pin_1
  BP PROBE 4: U1.P5, P10.MOUNT, R10.Pin_1
  INT: U1.INT, U2.INT, J1.pin4, Pad1.pad, Pad2.pad, Pad13.pad, Pad14.pad
  SCL: U1.SCL, U2.SCL, J1.pin3, Pad3.pad, Pad4.pad
  SDA: U1.SDA, U2.SDA, J1.pin2, Pad5.pad, Pad6.pad
  BP SCENE 4: U2.P0, P4.MOUNT, R4.Pin_1
  BP SCENE 3: U2.P1, P3.MOUNT, R3.Pin_1
  BP ZERO TRAVAIL: U2.P2, P12.MOUNT, R12.Pin_1
  BP ZERO Z: U2.P3, P11.MOUNT, R11.Pin_1
  BP SCENE 6: U2.P4, P6.MOUNT, R6.Pin_1, Pad11.pad, Pad12.pad
  BP SCENE 5: U2.P5, P5.MOUNT, R5.Pin_1, Pad9.pad, Pad10.pad

notes:
  +
  BY SMHOSY
  CANDLE-BLE
  BP SCENE

custom parts:
  MY PAD: StarbBoard Power pad Power pads are designated by the star cutout in the top layer.
