# Fritzing sketch CANDLE-BLE-FEED (saved by Fritzing 0.9.10b)
circuit board: 3.59999cm x 8.50001cm
breadboards: 1

parts:
  U1 = PCF8574 [package="DIP16 [THT]"]
  LED6 = LED - 3mm [color="Blue (430nm)" current=0.030 package="3 mm [THT]"]
  LED4 = LED - 3mm [color="Blue (430nm)" current=0.030 package="3 mm [THT]"]
  LED5 = LED - 3mm [color="Blue (430nm)" current=0.030 package="3 mm [THT]"]
  LED2 = LED - 3mm [color="Blue (430nm)" current=0.030 package="3 mm [THT]"]
  LED1 = LED - 3mm [color="Blue (430nm)" current=0.030 package="3 mm [THT]"]
  LED3 = LED - 3mm [color="Blue (430nm)" current=0.030 package="3 mm [THT]"]
  R3 = Resistor [tolerance=±5% resistance=680 power=0.25 package="1206 [SMD]"]
  R2 = Resistor [tolerance=±5% resistance=680 power=0.25 package="1206 [SMD]"]
  R4 = Resistor [tolerance=±5% resistance=680 power=0.25 package="1206 [SMD]"]
  R1 = Resistor [tolerance=±5% resistance=680 power=0.25 package="1206 [SMD]"]
  R5 = Resistor [tolerance=±5% resistance=680 power=0.25 package="1206 [SMD]"]
  J1 = double row smd male pin header, 6 pins [form="♂ (male)"]
  R6 = Resistor [tolerance=±5% resistance=680 power=0.25 package="1206 [SMD]"]
  P1-2 = MY PAD [package=NONE]
  P2 = MY PAD [package=NONE]
  R7 = Resistor [tolerance=±5% resistance=10k power=0.25 package="1206 [SMD]"]
  Pad1 = Pad [width=1 height=2 connect=center]
  Pad2 = Pad [width=1 height=2 connect=center]
  Pad3 = Pad [width=0.1 height=0.1 connect=center]  # not connected
  Pad4 = Pad [width=0.1 height=0.1 connect=center]  # not connected

nets:
  3.3V: U1.A0, U1.VCC, R3.Pin_1, R2.Pin_1, R4.Pin_1, R1.Pin_1, R5.Pin_1, J1.pin1, R6.Pin_1, R7.Pin_1
  GND: U1.A1, U1.A2, U1.GND, J1.pin6, P1-2.MOUNT
  FEED 10: U1.P1, LED6.cathode
  FEED 50: U1.P2, LED5.cathode
  FEED 100: U1.P3, LED4.cathode
  FEED 500: U1.P4, LED3.cathode
  FEED 1000: U1.P5, LED2.cathode
  FEED 2000: U1.P6, LED1.cathode
  BP_FEED: U1.P7, P2.MOUNT, R7.Pin_0
  INT: U1.INT, J1.pin4
  SCL: U1.SCL, J1.pin3, Pad1.pad, Pad2.pad
  SDA: U1.SDA, J1.pin2
  N1: LED6.anode, R6.Pin_0
  N2: LED4.anode, R4.Pin_0
  N3: LED5.anode, R5.Pin_0
  N4: LED2.anode, R2.Pin_0
  N5: LED1.anode, R1.Pin_0
  N6: LED3.anode, R3.Pin_0

notes:
  CANDLE-BLE FEED
  BY SMHOSY
  +

custom parts:
  MY PAD: StarbBoard Power pad Power pads are designated by the star cutout in the top layer.
