# Fritzing sketch CANDLE-BLE-SCENES (saved by Fritzing 0.9.10b)
circuit board: 14.6cm x 2.5cm
breadboards: 1

parts:
  U1 = PCF8574 [package="DIP16 [THT]"]
  LED1 = LED - 3mm [color="Blue (525nm)" current=0.030 package="3 mm [THT]"]
  LED2 = LED - 3mm [color="Blue (525nm)" current=0.030 package="3 mm [THT]"]
  LED3 = LED - 3mm [color="Blue (525nm)" current=0.030 package="3 mm [THT]"]
  LED4 = LED - 3mm [color="Blue (525nm)" current=0.030 package="3 mm [THT]"]
  LED5 = LED - 3mm [color="Blue (525nm)" current=0.030 package="3 mm [THT]"]
  LED6 = LED - 3mm [color="Blue (525nm)" current=0.030 package="3 mm [THT]"]
  R1 = Resistor [tolerance=±5% resistance=680 power=0.25 package="1206 [SMD]"]
  J1 = double row smd male pin header, 6 pins [form="♂ (male)"]
  R2 = Resistor [tolerance=±5% resistance=680 power=0.25 package="1206 [SMD]"]
  R3 = Resistor [tolerance=±5% resistance=680 power=0.25 package="1206 [SMD]"]
  R4 = Resistor [tolerance=±5% resistance=680 power=0.25 package="1206 [SMD]"]
  R5 = Resistor [tolerance=±5% resistance=680 power=0.25 package="1206 [SMD]"]
  R6 = Resistor [tolerance=±5% resistance=680 power=0.25 package="1206 [SMD]"]
  Pad1 = Pad [width=1 height=2 connect=center]
  Pad2 = Pad [width=1 height=2 connect=center]

nets:
  3.3V: U1.A0, U1.A2, U1.VCC, R1.Pin_1, J1.pin1, R2.Pin_1, R3.Pin_1, R4.Pin_1, R5.Pin_1, R6.Pin_1
  GND: U1.A1, U1.GND, J1.pin6, Pad1.pad, Pad2.pad
  LED SCENE 1: U1.P0, LED1.cathode
  LED SCENE 2: U1.P1, LED2.cathode
  LED SCENE 3: U1.P2, LED3.cathode
  LED SCENE 4: U1.P3, LED4.cathode
  LED SCENE 5: U1.P4, LED5.cathode
  LED SCENE 6: U1.P5, LED6.cathode
  SCL: U1.SCL, J1.pin3
  SDA: U1.SDA, J1.pin2
  N1: LED1.anode, R1.Pin_0
  N2: LED2.anode, R2.Pin_0
  N3: LED3.anode, R3.Pin_0
  N4: LED4.anode, R4.Pin_0
  N5: LED5.anode, R5.Pin_0
  N6: LED6.anode, R6.Pin_0

notes:
  BY SMHOSY
  CANDLE-BLE SCENE
  +
